# Fritzing sketch Polisher (saved by Fritzing 0.9.6b)

parts:
  Bauteil1 = Arduino Nano (Rev3.0)
  DRV_1 = DRV 8825 Stepper Motor Carrier, High Current [part_number="DRV 8825"]
  M2 = Stepper Motor - Bipolar
  J1 = Power Jack [package=power_jack_pth]
  C1 = Capacitor Polarized [package=cpol-radial-100uf-25v]
  R1 = Rotary Potentiometer (Large) [maximum_resistance=10kΩ package=THT]

nets:
  N1: Bauteil1.GND, DRV_1.ENABLE, DRV_1.MS3, DRV_1.GROUND_ST/_MT, DRV_1.GROUND_LOG, J1.GNDBREAK, C1.-, R1.leg2
  N2: Bauteil1.D2, DRV_1.RESET
  N3: Bauteil1.D3, DRV_1.SLEEP
  N4: Bauteil1.D4, DRV_1.STEP
  N5: Bauteil1.D5, DRV_1.DIRECTION
  VIN: Bauteil1.VIN, DRV_1.MS1, DRV_1.MS2, DRV_1.VOLTAGE_ST/_MT, J1.GND, C1.+
  N6: Bauteil1.5V, R1.leg1
  N7: Bauteil1.A0, R1.wiper
  N8: DRV_1.OUT_2B, M2.A
  N9: DRV_1.OUT_2A, M2.C
  N10: DRV_1.OUT_1A, M2.B
  N11: DRV_1.OUT_1B, M2.D
